# Fritzing sketch fake_bomb_schematic (saved by Fritzing 0.9.6b)
breadboards: 1

parts:
  Arduino = Arduino Uno (Rev3)
  LCD1 = Adafruit Positive RGB 2x16 LCD

nets:
  N1: Arduino.GND, LCD1.no_name_yet#0, LCD1.no_name_yet#4
  N2: Arduino.5V, LCD1.no_name_yet#1, LCD1.no_name_yet#14

custom parts:
  Adafruit Positive RGB 2x16 LCD: Adafruit Positive 2x16 LCD Display with RGB Backlight
